// Logisim project lab2.circ as structural Verilog: 5 circuits, main circuit Circuit B
module Circuit_A (
  input  A,
  input  B,
  input  C,
  output Output
);

  wire and_1_out, and_2_out, not_1_out, not_2_out, not_3_out;

  and and_1 (and_1_out, A, B, C);
  not not_1 (not_1_out, C);
  not not_2 (not_2_out, B);
  not not_3 (not_3_out, A);
  and and_2 (and_2_out, not_1_out, not_2_out, not_3_out);
  or or_1 (Output, and_1_out, and_2_out);

  // Notes on the sheet:
  //   Circuit A: (ABC) + (~A.~B.~C)
  //   ~A
  //   ~B
  //   ~C
  //   ABC
  //   ~A~B~C
endmodule

module Circuit_B (
  input  A,
  input  B,
  input  C,
  output Output
);

  wire and_1_out, and_2_out, and_3_out, not_1_out, not_2_out, not_3_out;

  not not_1 (not_1_out, C);
  not not_2 (not_2_out, B);
  and and_1 (and_1_out, A, B, C);
  not not_3 (not_3_out, A);
  and and_2 (and_2_out, not_1_out, not_2_out, A);
  and and_3 (and_3_out, not_3_out, not_2_out, not_1_out);
  or or_1 (Output, and_1_out, and_2_out, and_3_out);

  // Notes on the sheet:
  //   Circuit B: (ABC) + (A.~B.~C) + (~A.~B.~C)
  //   ~B
  //   ABC
  //   ~C
  //   ~A
  //   A~B~C
  //   ~A~B~C
endmodule

module Circuit_C (
  input  A,
  input  B,
  input  C,
  output X
);

  wire and_1_out, and_2_out, not_1_out, not_2_out, or_1_out;

  not not_1 (not_1_out, C);
  not not_2 (not_2_out, B);
  and and_1 (and_1_out, B, not_1_out);
  and and_2 (and_2_out, C, not_2_out);
  or or_1 (or_1_out, and_2_out, and_1_out);
  and and_3 (X, A, or_1_out);

  // Notes on the sheet:
  //   Circuit C: A.((B.~C) + (~B.C))
  //   ~C
  //   ~B
  //   B~C
  //   ~BC
  //   (~B.C) + (B.~C)
  //   Output
endmodule

module Circuit_D (
  input  A,
  input  B,
  input  C,
  output Output
);

  wire and_1_out, and_2_out, not_1_out, or_1_out;

  and and_1 (and_1_out, A, B, C);
  or or_1 (or_1_out, C, B);
  not not_1 (not_1_out, or_1_out);
  and and_2 (and_2_out, not_1_out, A);
  or or_2 (Output, and_1_out, and_2_out);

  // Notes on the sheet:
  //   Circuit D: (ABC) + (A.~(B + C))
  //   B+C
  //   ABC
  //   ~ B+C
  //   A ~B+C
endmodule

module Circuit_E (
  input  A,
  input  B,
  input  C,
  output Ouput
);

  wire not_1_out, not_2_out, or_1_out, or_2_out, or_3_out;

  or or_1 (or_1_out, A, B);
  not not_1 (not_1_out, B);
  not not_2 (not_2_out, A);
  or or_2 (or_2_out, A, C);
  or or_3 (or_3_out, not_1_out, not_2_out);
  and and_1 (Ouput, or_1_out, or_3_out, or_2_out);

  // Notes on the sheet:
  //   Circuit E: (A + B).(A + C).(~A + ~B)
  //   ~A
  //   ~B
  //   A+B
  //   A+C
  //   ~A+~B
endmodule
